// Logisim project main.circ as structural Verilog
module MIPS32 (
);

  wire and_2_out, clock_1_out, compare_1_out, control_1_alusrc, control_1_branch, control_1_comp,
       control_1_compselect, control_1_lui, control_1_memread, control_1_memtoreg, control_1_memwrite,
       control_1_mov, control_1_regdst, control_1_regwrite, control_1_shamtchoose, control_1_zeroextend,
       ex_mem_pipeline_register_1_regwrite_2, id_ex_pipeline_register_1_alusrc_2,
       id_ex_pipeline_register_1_comp_2, id_ex_pipeline_register_1_compselect_2,
       id_ex_pipeline_register_1_mov_2, id_ex_pipeline_register_1_regwrite_2, multiplexer_8_out, not_1_out,
       registerfile_1_p3;
  wire [1:0] forwardctrl_1_fa, forwardctrl_1_fb;
  wire [3:0] control_1_alu_op, id_ex_pipeline_register_1_aluop_2;
  wire [4:0] ex_mem_pipeline_register_1_regwriteaddress_2, ex_mem_pipeline_register_1_result_2,
       id_ex_pipeline_register_1_rs_2, id_ex_pipeline_register_1_rt_2, id_ex_pipeline_register_1_shamt_2,
       id_ex_pipeline_register_1_writeregaddress_2, if_id_pipeline_register_1_instruction_2_2,
       if_id_pipeline_register_1_instruction_2_4, multiplexer_1_out, multiplexer_6_out, registerfile_1_p4,
       shamt_1_shamt;
  wire [5:0] if_id_pipeline_register_1_instruction_2;
  wire [15:11] if_id_pipeline_register_1_instruction_2_3;
  wire [31:0] and_1_out, bit_extender_1_out, bit_extender_2_out, bit_extender_3_out, bit_extender_4_out,
       fetch_sub_1_out, id_ex_pipeline_register_1_imm_2, id_ex_pipeline_register_1_readdata1_2,
       id_ex_pipeline_register_1_readdata2_2, mips_alu_1_p5, mipsprogramrom_1_p2, multiplexer_2_out,
       multiplexer_3_out, multiplexer_4_out, multiplexer_5_out, multiplexer_7_out, multiplexer_9_out,
       registerfile_1_p1, registerfile_1_p7, registerfile_1_p8;
  wire [31:5] ex_mem_pipeline_register_1_result_2_2;
  wire [31:21] if_id_pipeline_register_1_instruction_2_5;

  Clock clock_1 (.out(clock_1_out));
  Fetch_Sub fetch_sub_1 (.Clock(clock_1_out), .Out(fetch_sub_1_out));
  // MIPSProgramROM mipsprogramrom_1: pin names not known; wires that end beside it: fetch_sub_1_out, mipsprogramrom_1_p2
  IF_ID_Pipeline_Register if_id_pipeline_register_1 (
    .PC_4(fetch_sub_1_out), .Instruction(mipsprogramrom_1_p2), .Clock(clock_1_out),
    .Instruction_2({if_id_pipeline_register_1_instruction_2_5, if_id_pipeline_register_1_instruction_2_4, if_id_pipeline_register_1_instruction_2_3, if_id_pipeline_register_1_instruction_2_2, if_id_pipeline_register_1_instruction_2}));  // open: PC_4_2
  // RegisterFile registerfile_1: pin names not known; wires that end beside it: registerfile_1_p1, clock_1_out, registerfile_1_p3, registerfile_1_p4, if_id_pipeline_register_1_instruction_2_5[25:21], if_id_pipeline_register_1_instruction_2_4, registerfile_1_p7, registerfile_1_p8
  Control control_1 (
    .Bit_16(if_id_pipeline_register_1_instruction_2_4[0]),
    .Op_Code(if_id_pipeline_register_1_instruction_2_5[31:26]),
    .func(if_id_pipeline_register_1_instruction_2), .ALU_Op(control_1_alu_op), .RegDst(control_1_regdst),
    .MemRead(control_1_memread), .MemtoReg(control_1_memtoreg), .Memwrite(control_1_memwrite),
    .ALUsrc(control_1_alusrc), .RegWrite(control_1_regwrite), .Branch(control_1_branch),
    .Comp(control_1_comp), .CompSelect(control_1_compselect), .LUI(control_1_lui),
    .Shamtchoose(control_1_shamtchoose), .MOV(control_1_mov), .Zeroextend(control_1_zeroextend));
  Multiplexer #(.width(5)) multiplexer_1 (
    .in0(if_id_pipeline_register_1_instruction_2_4), .in1(if_id_pipeline_register_1_instruction_2_3),
    .out(multiplexer_1_out), .sel(control_1_regdst));  // open: en
  assign bit_extender_1_out = {{16{if_id_pipeline_register_1_instruction_2_3[15]}}, {if_id_pipeline_register_1_instruction_2_3, if_id_pipeline_register_1_instruction_2_2, if_id_pipeline_register_1_instruction_2}};  // Bit_Extender bit_extender_1
  assign bit_extender_2_out = {{16{1'b0}}, {if_id_pipeline_register_1_instruction_2_3, if_id_pipeline_register_1_instruction_2_2, if_id_pipeline_register_1_instruction_2}};  // Bit_Extender bit_extender_2
  Shamt shamt_1 (
    .LUI(control_1_lui), .Shamtchoose(control_1_shamtchoose), .A(if_id_pipeline_register_1_instruction_2_2),
    ._6_10(registerfile_1_p7[4:0]), .Shamt(shamt_1_shamt));
  Multiplexer #(.width(32)) multiplexer_2 (
    .in0(bit_extender_1_out), .in1(bit_extender_2_out), .out(multiplexer_2_out), .sel(control_1_zeroextend));  // open: en
  ID_EX_Pipeline_Register id_ex_pipeline_register_1 (
    .ALUOp(control_1_alu_op), .Branch(control_1_branch), .RegWrite(control_1_regwrite),
    .WriteRegAddress(multiplexer_1_out), .MemRead(control_1_memread), .MemtoReg(control_1_memtoreg),
    .MemWrite(control_1_memwrite), .Clock(clock_1_out), .ReadData1(registerfile_1_p7),
    .ReadData2(registerfile_1_p8), .Shamt(shamt_1_shamt), .ALUOp_2(id_ex_pipeline_register_1_aluop_2),
    .RegWrite_2(id_ex_pipeline_register_1_regwrite_2),
    .WriteRegAddress_2(id_ex_pipeline_register_1_writeregaddress_2),
    .ReadData1_2(id_ex_pipeline_register_1_readdata1_2), .ReadData2_2(id_ex_pipeline_register_1_readdata2_2),
    .Shamt_2(id_ex_pipeline_register_1_shamt_2), .Comp_2(id_ex_pipeline_register_1_comp_2),
    .Comp(control_1_comp), .CompSelect(control_1_compselect),
    .CompSelect_2(id_ex_pipeline_register_1_compselect_2), .Mov_2(id_ex_pipeline_register_1_mov_2),
    .Mov(control_1_mov), .Imm(multiplexer_2_out), .Imm_2(id_ex_pipeline_register_1_imm_2),
    .ALUSrc(control_1_alusrc), .ALUSrc_2(id_ex_pipeline_register_1_alusrc_2),
    .Rs_2(id_ex_pipeline_register_1_rs_2), .Rs(if_id_pipeline_register_1_instruction_2_5[25:21]),
    .Rt(if_id_pipeline_register_1_instruction_2_4), .Rt_2(id_ex_pipeline_register_1_rt_2));  // open: Branch_2, MemRead_2, MemtoReg_2, MemWrite_2
  Multiplexer #(.select(2), .width(32)) multiplexer_3 (
    .in0(id_ex_pipeline_register_1_readdata1_2), .in1(registerfile_1_p1),
    .in2({ex_mem_pipeline_register_1_result_2_2, ex_mem_pipeline_register_1_result_2}),
    .out(multiplexer_3_out), .sel(forwardctrl_1_fa));  // open: in3, en
  Multiplexer #(.select(2), .width(32)) multiplexer_4 (
    .in0(id_ex_pipeline_register_1_readdata2_2), .in1(registerfile_1_p1),
    .in2({ex_mem_pipeline_register_1_result_2_2, ex_mem_pipeline_register_1_result_2}),
    .out(multiplexer_4_out), .sel(forwardctrl_1_fb));  // open: in3, en
  not not_1 (not_1_out, id_ex_pipeline_register_1_mov_2);
  Multiplexer #(.width(32)) multiplexer_5 (
    .in0(multiplexer_4_out), .in1(id_ex_pipeline_register_1_imm_2), .out(multiplexer_5_out),
    .sel(id_ex_pipeline_register_1_alusrc_2));  // open: en
  ForwardCtrl forwardctrl_1 (
    .XMRegWrite(ex_mem_pipeline_register_1_regwrite_2), .MWRegWrite(registerfile_1_p3),
    .XMRd(ex_mem_pipeline_register_1_regwriteaddress_2), .DXRs(id_ex_pipeline_register_1_rs_2),
    .DXRt(id_ex_pipeline_register_1_rt_2), .MWRd(registerfile_1_p4), .FA(forwardctrl_1_fa),
    .FB(forwardctrl_1_fb));
  assign bit_extender_3_out = {{31{not_1_out}}, not_1_out};  // Bit_Extender bit_extender_3
  assign and_1_out = bit_extender_3_out & multiplexer_3_out;  // AND_Gate and_1, 32 bits wide
  Multiplexer #(.select(2), .width(5)) multiplexer_6 (
    .in0(id_ex_pipeline_register_1_shamt_2), .in1(registerfile_1_p1[4:0]),
    .in2(ex_mem_pipeline_register_1_result_2), .out(multiplexer_6_out), .sel(forwardctrl_1_fa));  // open: in3, en
  Compare compare_1 (
    .A(multiplexer_3_out), .B(multiplexer_5_out), .Selector(id_ex_pipeline_register_1_compselect_2),
    .Out(compare_1_out));
  // Mips_ALU mips_alu_1: pin names not known; wires that end beside it: and_1_out, multiplexer_5_out, id_ex_pipeline_register_1_aluop_2, multiplexer_6_out, mips_alu_1_p5
  assign bit_extender_4_out = {{31{1'b0}}, compare_1_out};  // Bit_Extender bit_extender_4
  and and_2 (and_2_out, id_ex_pipeline_register_1_regwrite_2, mips_alu_1_p5[0]);
  Multiplexer #(.width(32)) multiplexer_7 (
    .in0(mips_alu_1_p5), .in1(bit_extender_4_out), .out(multiplexer_7_out),
    .sel(id_ex_pipeline_register_1_comp_2));  // open: en
  Multiplexer multiplexer_8 (
    .in0(id_ex_pipeline_register_1_regwrite_2), .in1(and_2_out), .out(multiplexer_8_out),
    .sel(id_ex_pipeline_register_1_mov_2));  // open: en
  Multiplexer #(.width(32)) multiplexer_9 (
    .in0(multiplexer_7_out), .in1(multiplexer_3_out), .out(multiplexer_9_out),
    .sel(id_ex_pipeline_register_1_mov_2));  // open: en
  EX_MEM_Pipeline_Register ex_mem_pipeline_register_1 (
    .RegWrite(multiplexer_8_out), .RegWriteAddress(id_ex_pipeline_register_1_writeregaddress_2),
    .Result(multiplexer_9_out), .Clock(clock_1_out), .RegWrite_2(ex_mem_pipeline_register_1_regwrite_2),
    .RegWriteAddress_2(ex_mem_pipeline_register_1_regwriteaddress_2),
    .Result_2({ex_mem_pipeline_register_1_result_2_2, ex_mem_pipeline_register_1_result_2}));
  EX_WB_Pipeline_Register ex_wb_pipeline_register_1 (
    .RegWrite(ex_mem_pipeline_register_1_regwrite_2),
    .RegWriteAddress(ex_mem_pipeline_register_1_regwriteaddress_2),
    .Result({ex_mem_pipeline_register_1_result_2_2, ex_mem_pipeline_register_1_result_2}),
    .Clock(clock_1_out), .RegWrite_2(registerfile_1_p3), .RegWriteAddress_2(registerfile_1_p4),
    .Result_2(registerfile_1_p1));
endmodule

module PC_Inc (
  input  [31:0] Input,
  output [31:0] Output
);

  // Incrementer incrementer_1: pin names not known; wires that end beside it: Input[31:2], Output[31:2]

  assign Output[1:0] = Input[1:0];
endmodule

// PC+4
module Fetch_Sub (
  input  Clock,
  output [31:0] Out
);

  wire [31:0] pc_inc_1_output;

  Register #(.width(32)) register_1 (.D(pc_inc_1_output), .Q(Out), .clk(Clock));  // open: en, clr
  PC_Inc pc_inc_1 (.Input(Out), .Output(pc_inc_1_output));
endmodule

// IF/ID
module IF_ID_Pipeline_Register (
  input  [31:0] PC_4,
  input  [31:0] Instruction,
  input  Clock,
  output [31:0] PC_4_2,
  output [31:0] Instruction_2
);

  Register #(.width(32)) u_PC_4 (.D(PC_4), .Q(PC_4_2), .clk(Clock));  // open: en, clr
  Register #(.width(32)) u_Instruction (.D(Instruction), .Q(Instruction_2), .clk(Clock));  // open: en, clr
endmodule

// OP ctrl
module OpCtrl (
  input  Op5,
  input  Op4,
  input  Op3,
  input  Op2,
  input  Op1,
  input  Op0,
  output RegDst,
  output Branch,
  output MemRead,
  output MemToReg,
  output MemWrite,
  output ALUsr,
  output RegWrite,
  output Special,
  output Regimm,
  output Comp,
  output CompSelect,
  output Lui,
  output Zeroextend
);

  wire and_2_out, and_3_out, and_4_out, and_5_out, and_6_out, and_7_out, and_8_out, and_9_out, and_10_out,
       and_11_out, and_12_out, and_13_out, and_14_out, and_15_out, and_16_out, and_17_out, and_18_out,
       and_19_out, not_1_out, not_2_out, not_3_out, not_4_out, not_5_out, not_6_out, not_7_out, not_8_out,
       not_9_out, not_10_out, not_11_out, not_12_out, not_13_out, not_14_out, not_15_out, not_16_out,
       not_17_out, not_18_out, not_19_out, not_20_out, not_21_out, not_22_out, not_23_out, not_24_out,
       not_25_out, not_26_out, not_27_out, not_28_out, not_29_out, not_30_out, not_31_out, not_32_out,
       not_33_out, not_34_out, not_35_out, not_36_out, not_37_out, not_38_out, not_39_out, not_40_out,
       not_41_out, not_42_out, not_43_out, not_44_out, not_45_out, not_46_out, not_47_out, not_48_out,
       not_49_out, not_50_out, not_51_out, not_52_out, not_53_out, not_54_out, not_55_out, not_56_out,
       not_57_out, not_58_out, not_59_out, not_60_out, not_61_out, not_62_out, not_63_out, not_64_out,
       not_65_out, not_66_out, not_67_out, not_68_out, not_69_out, not_70_out, not_71_out, not_72_out;

  not not_1 (not_1_out, Op5);
  not not_2 (not_2_out, Op4);
  not not_3 (not_3_out, Op3);
  not not_4 (not_4_out, Op5);
  not not_5 (not_5_out, Op4);
  not not_6 (not_6_out, Op3);
  not not_7 (not_7_out, Op5);
  not not_8 (not_8_out, Op4);
  not not_9 (not_9_out, Op3);
  not not_10 (not_10_out, Op5);
  not not_11 (not_11_out, Op4);
  not not_12 (not_12_out, Op3);
  not not_13 (not_13_out, Op4);
  not not_14 (not_14_out, Op3);
  not not_15 (not_15_out, Op1);
  not not_16 (not_16_out, Op0);
  not not_17 (not_17_out, Op4);
  not not_18 (not_18_out, Op3);
  not not_19 (not_19_out, Op2);
  not not_20 (not_20_out, Op4);
  not not_21 (not_21_out, Op3);
  not not_22 (not_22_out, Op1);
  not not_23 (not_23_out, Op0);
  not not_24 (not_24_out, Op4);
  not not_25 (not_25_out, Op3);
  not not_26 (not_26_out, Op2);
  not not_27 (not_27_out, Op4);
  not not_28 (not_28_out, Op2);
  not not_29 (not_29_out, Op1);
  not not_30 (not_30_out, Op0);
  not not_31 (not_31_out, Op4);
  not not_32 (not_32_out, Op2);
  not not_33 (not_33_out, Op5);
  not not_34 (not_34_out, Op4);
  not not_35 (not_35_out, Op5);
  not not_36 (not_36_out, Op4);
  not not_37 (not_37_out, Op5);
  not not_38 (not_38_out, Op4);
  not not_39 (not_39_out, Op4);
  not not_40 (not_40_out, Op3);
  not not_41 (not_41_out, Op1);
  not not_42 (not_42_out, Op0);
  not not_43 (not_43_out, Op4);
  not not_44 (not_44_out, Op2);
  not not_45 (not_45_out, Op1);
  not not_46 (not_46_out, Op0);
  not not_47 (not_47_out, Op4);
  not not_48 (not_48_out, Op2);
  not not_49 (not_49_out, Op5);
  not not_50 (not_50_out, Op4);
  not not_51 (not_51_out, Op5);
  not not_52 (not_52_out, Op4);
  not not_53 (not_53_out, Op5);
  not not_54 (not_54_out, Op4);
  not not_55 (not_55_out, Op5);
  not not_56 (not_56_out, Op4);
  not not_57 (not_57_out, Op3);
  not not_58 (not_58_out, Op2);
  not not_59 (not_59_out, Op1);
  not not_60 (not_60_out, Op0);
  not not_61 (not_61_out, Op5);
  not not_62 (not_62_out, Op4);
  not not_63 (not_63_out, Op3);
  not not_64 (not_64_out, Op2);
  not not_65 (not_65_out, Op1);
  not not_66 (not_66_out, Op5);
  not not_67 (not_67_out, Op4);
  not not_68 (not_68_out, Op2);
  not not_69 (not_69_out, Op5);
  not not_70 (not_70_out, Op4);
  not not_71 (not_71_out, Op5);
  not not_72 (not_72_out, Op4);
  and and_1 (RegDst, not_1_out, not_2_out, not_3_out, Op2);
  and and_2 (and_2_out, not_4_out, not_5_out, not_6_out, Op0);
  and and_3 (and_3_out, not_7_out, not_8_out, not_9_out, Op1);
  and and_4 (and_4_out, not_10_out, not_11_out, not_12_out, Op2);
  and and_5 (and_5_out, Op5, not_13_out, not_14_out, not_15_out, not_16_out);
  and and_6 (and_6_out, Op5, not_17_out, not_18_out, not_19_out, Op1, Op0);
  and and_7 (and_7_out, Op5, not_20_out, not_21_out, not_22_out, not_23_out);
  and and_8 (and_8_out, Op5, not_24_out, not_25_out, not_26_out, Op1, Op0);
  and and_9 (and_9_out, Op5, not_27_out, Op3, not_28_out, not_29_out, not_30_out);
  and and_10 (and_10_out, Op5, not_31_out, Op3, not_32_out, Op1, Op0);
  and and_11 (and_11_out, not_33_out, not_34_out, Op3, Op0);
  and and_12 (and_12_out, not_35_out, not_36_out, Op3, Op1);
  and and_13 (and_13_out, not_37_out, not_38_out, Op3, Op2);
  and and_14 (and_14_out, Op5, not_39_out, not_40_out, not_41_out, not_42_out);
  and and_15 (and_15_out, Op5, not_43_out, not_44_out, not_45_out, not_46_out);
  and and_16 (and_16_out, Op5, not_47_out, not_48_out, Op1, Op0);
  and and_17 (and_17_out, not_49_out, not_50_out, Op3, Op0);
  and and_18 (and_18_out, not_51_out, not_52_out, Op3, Op1);
  and and_19 (and_19_out, not_53_out, not_54_out, Op3, Op2);
  and and_20 (Special, not_55_out, not_56_out, not_57_out, not_58_out, not_59_out, not_60_out);
  and and_21 (Regimm, not_61_out, not_62_out, not_63_out, not_64_out, not_65_out, Op0);
  and and_22 (Comp, not_66_out, not_67_out, Op3, not_68_out, Op1);
  and and_23 (Lui, not_69_out, not_70_out, Op3, Op2, Op1, Op0);
  and and_24 (Zeroextend, not_71_out, not_72_out, Op3, Op2);
  or or_1 (Branch, and_2_out, and_3_out, and_4_out);
  or or_2 (MemRead, and_5_out, and_6_out);
  or or_3 (MemToReg, and_7_out, and_8_out);
  or or_4 (MemWrite, and_9_out, and_10_out);
  or or_5 (ALUsr, and_11_out, and_12_out, and_13_out, and_14_out, and_15_out, and_16_out);
  or or_6 (RegWrite, and_17_out, and_18_out, and_19_out);

  assign CompSelect = Op0;
endmodule

module Special_Ctrl (
  input  Func5,
  input  Func4,
  input  Func3,
  input  Func2,
  input  Func1,
  input  Func0,
  output RegDST,
  output Branch,
  output RegWrite,
  output Comp,
  output CompSelect,
  output ShamtChoose,
  output MOV
);

  wire and_1_out, and_2_out, and_3_out, and_4_out, and_5_out, and_6_out, and_8_out, and_9_out, and_10_out,
       and_11_out, and_12_out, not_1_out, not_2_out, not_3_out, not_4_out, not_5_out, not_6_out, not_7_out,
       not_8_out, not_9_out, not_10_out, not_11_out, not_12_out, not_13_out, not_14_out, not_15_out,
       not_16_out, not_17_out, not_18_out, not_19_out, not_20_out, not_21_out, not_22_out, not_23_out,
       not_24_out, not_25_out, not_26_out, not_27_out, not_28_out, not_29_out, not_30_out, not_31_out,
       not_32_out, not_33_out, not_34_out, not_35_out, not_36_out, not_37_out, not_38_out;

  not not_1 (not_1_out, Func5);
  not not_2 (not_2_out, Func4);
  not not_3 (not_3_out, Func3);
  not not_4 (not_4_out, Func0);
  not not_5 (not_5_out, Func4);
  not not_6 (not_6_out, Func3);
  not not_7 (not_7_out, Func4);
  not not_8 (not_8_out, Func3);
  not not_9 (not_9_out, Func0);
  not not_10 (not_10_out, Func5);
  not not_11 (not_11_out, Func4);
  not not_12 (not_12_out, Func2);
  not not_13 (not_13_out, Func4);
  not not_14 (not_14_out, Func2);
  not not_15 (not_15_out, Func4);
  not not_16 (not_16_out, Func3);
  not not_17 (not_17_out, Func5);
  not not_18 (not_18_out, Func4);
  not not_19 (not_19_out, Func2);
  not not_20 (not_20_out, Func1);
  not not_21 (not_21_out, Func5);
  not not_22 (not_22_out, Func4);
  not not_23 (not_23_out, Func3);
  not not_24 (not_24_out, Func0);
  not not_25 (not_25_out, Func4);
  not not_26 (not_26_out, Func3);
  not not_27 (not_27_out, Func4);
  not not_28 (not_28_out, Func3);
  not not_29 (not_29_out, Func0);
  not not_30 (not_30_out, Func4);
  not not_31 (not_31_out, Func2);
  not not_32 (not_32_out, Func4);
  not not_33 (not_33_out, Func3);
  not not_34 (not_34_out, Func4);
  not not_35 (not_35_out, Func2);
  not not_36 (not_36_out, Func5);
  not not_37 (not_37_out, Func4);
  not not_38 (not_38_out, Func2);
  and and_1 (and_1_out, not_1_out, not_2_out, not_3_out, not_4_out);
  and and_2 (and_2_out, not_5_out, not_6_out, Func1, Func0);
  and and_3 (and_3_out, not_7_out, not_8_out, Func2, not_9_out);
  and and_4 (and_4_out, not_10_out, not_11_out, Func3, not_12_out, Func0);
  and and_5 (and_5_out, not_13_out, Func3, not_14_out, Func1);
  and and_6 (and_6_out, Func5, not_15_out, not_16_out, Func0);
  and and_7 (Branch, not_17_out, not_18_out, Func3, not_19_out, not_20_out);
  and and_8 (and_8_out, not_21_out, not_22_out, not_23_out, not_24_out);
  and and_9 (and_9_out, not_25_out, not_26_out, Func1, Func0);
  and and_10 (and_10_out, not_27_out, not_28_out, Func2, not_29_out);
  and and_11 (and_11_out, not_30_out, Func3, not_31_out, Func1);
  and and_12 (and_12_out, Func5, not_32_out, not_33_out, Func0);
  and and_13 (Comp, Func5, not_34_out, Func3, not_35_out, Func1);
  and and_14 (MOV, not_36_out, not_37_out, Func3, not_38_out, Func1);
  or or_1 (RegDST, and_1_out, and_2_out, and_3_out, and_4_out, and_5_out, and_6_out);
  or or_2 (RegWrite, and_8_out, and_9_out, and_10_out, and_11_out, and_12_out);

  assign CompSelect = Func0;
  assign ShamtChoose = Func2;
endmodule

module Control (
  input  Bit_16,
  input  [5:0] Op_Code,
  input  [5:0] func,
  output [3:0] ALU_Op,
  output RegDst,
  output MemRead,
  output MemtoReg,
  output Memwrite,
  output ALUsrc,
  output RegWrite,
  output Branch,
  output Comp,
  output CompSelect,
  output LUI,
  output Shamtchoose,
  output MOV,
  output Zeroextend
);

  wire opctrl_1_branch, opctrl_1_comp, opctrl_1_compselect, opctrl_1_regdst, opctrl_1_regimm,
       opctrl_1_regwrite, opctrl_1_special, special_ctrl_1_branch, special_ctrl_1_comp,
       special_ctrl_1_compselect, special_ctrl_1_mov, special_ctrl_1_regdst, special_ctrl_1_regwrite;
  wire [3:0] alu_op_ctrl_1_alu0, alu_regimm_ctrl_1_alu_op, alu_special_ctrl_1_alu0, multiplexer_1_out;

  OpCtrl opctrl_1 (
    .Op5(Op_Code[5]), .Op4(Op_Code[4]), .Op3(Op_Code[3]), .Op2(Op_Code[2]), .Op1(Op_Code[1]),
    .Op0(Op_Code[0]), .RegDst(opctrl_1_regdst), .Branch(opctrl_1_branch), .MemRead(MemRead),
    .MemToReg(MemtoReg), .MemWrite(Memwrite), .ALUsr(ALUsrc), .RegWrite(opctrl_1_regwrite),
    .Special(opctrl_1_special), .Regimm(opctrl_1_regimm), .Comp(opctrl_1_comp),
    .CompSelect(opctrl_1_compselect), .Lui(LUI), .Zeroextend(Zeroextend));
  Special_Ctrl special_ctrl_1 (
    .Func5(func[5]), .Func4(func[4]), .Func3(func[3]), .Func2(func[2]), .Func1(func[1]), .Func0(func[0]),
    .RegDST(special_ctrl_1_regdst), .Branch(special_ctrl_1_branch), .RegWrite(special_ctrl_1_regwrite),
    .Comp(special_ctrl_1_comp), .CompSelect(special_ctrl_1_compselect), .ShamtChoose(Shamtchoose),
    .MOV(special_ctrl_1_mov));
  ALU_op_Ctrl alu_op_ctrl_1 (
    .Op5(Op_Code[5]), .Op4(Op_Code[4]), .Op3(Op_Code[3]), .Op2(Op_Code[2]), .Op1(Op_Code[1]),
    .Op0(Op_Code[0]), .ALU3(alu_op_ctrl_1_alu0[3]), .ALU2(alu_op_ctrl_1_alu0[2]),
    .ALU1(alu_op_ctrl_1_alu0[1]), .ALU0(alu_op_ctrl_1_alu0[0]));
  ALU_special_ctrl alu_special_ctrl_1 (
    .func5(func[5]), .func4(func[4]), .func3(func[3]), .func2(func[2]), .func1(func[1]), .func0(func[0]),
    .ALU3(alu_special_ctrl_1_alu0[3]), .ALU2(alu_special_ctrl_1_alu0[2]), .ALU1(alu_special_ctrl_1_alu0[1]),
    .ALU0(alu_special_ctrl_1_alu0[0]));
  ALU_Regimm_Ctrl alu_regimm_ctrl_1 (.Bit_16(Bit_16), .ALU_Op(alu_regimm_ctrl_1_alu_op));
  Multiplexer #(.width(4)) multiplexer_1 (
    .in0(alu_op_ctrl_1_alu0), .in1(alu_special_ctrl_1_alu0), .out(multiplexer_1_out), .sel(opctrl_1_special));  // open: en
  Multiplexer #(.width(4)) multiplexer_2 (
    .in0(multiplexer_1_out), .in1(alu_regimm_ctrl_1_alu_op), .out(ALU_Op), .sel(opctrl_1_regimm));  // open: en
  Multiplexer multiplexer_3 (
    .in0(opctrl_1_regdst), .in1(special_ctrl_1_regdst), .out(RegDst), .sel(opctrl_1_special));  // open: en
  Multiplexer multiplexer_4 (
    .in0(opctrl_1_regwrite), .in1(special_ctrl_1_regwrite), .out(RegWrite), .sel(opctrl_1_special));  // open: en
  Multiplexer multiplexer_5 (
    .in0(opctrl_1_branch), .in1(special_ctrl_1_branch), .out(Branch), .sel(opctrl_1_special));  // open: en
  Multiplexer multiplexer_6 (
    .in0(opctrl_1_comp), .in1(special_ctrl_1_comp), .out(Comp), .sel(opctrl_1_special));  // open: en
  Multiplexer multiplexer_7 (
    .in0(opctrl_1_compselect), .in1(special_ctrl_1_compselect), .out(CompSelect), .sel(opctrl_1_special));  // open: en
  and and_1 (MOV, opctrl_1_special, special_ctrl_1_mov);
endmodule

module Compare (
  input  [31:0] A,
  input  [31:0] B,
  input  Selector,
  output Out
);

  wire comparator_1_lt, comparator_2_lt;

  Comparator #(.width(32)) comparator_1 (.a(A), .b(B), .lt(comparator_1_lt));  // open: gt, eq
  Comparator #(.width(32), .mode("unsigned")) comparator_2 (.a(A), .b(B), .lt(comparator_2_lt));  // open: gt, eq
  Multiplexer multiplexer_1 (.in0(comparator_1_lt), .in1(comparator_2_lt), .out(Out), .sel(Selector));  // open: en
endmodule

// ALU Op Ctrl
module ALU_op_Ctrl (
  input  Op5,
  input  Op4,
  input  Op3,
  input  Op2,
  input  Op1,
  input  Op0,
  output ALU3,
  output ALU2,
  output ALU1,
  output ALU0
);

  wire and_1_out, and_2_out, and_3_out, and_4_out, and_5_out, and_6_out, and_7_out, and_8_out, and_9_out,
       and_10_out, and_11_out, and_12_out, and_13_out, and_14_out, and_15_out, and_16_out, and_17_out,
       not_1_out, not_2_out, not_3_out, not_4_out, not_5_out, not_6_out, not_7_out, not_8_out, not_9_out,
       not_10_out, not_11_out, not_12_out, not_13_out, not_14_out, not_15_out, not_16_out, not_17_out,
       not_18_out, not_19_out, not_20_out, not_21_out, not_22_out, not_23_out, not_24_out, not_25_out,
       not_26_out, not_27_out, not_28_out, not_29_out, not_30_out, not_31_out, not_32_out, not_33_out,
       not_34_out, not_35_out, not_36_out, not_37_out, not_38_out, not_39_out, not_40_out, not_41_out,
       not_42_out, not_43_out, not_44_out, not_45_out, not_46_out, not_47_out, not_48_out, not_49_out,
       not_50_out, not_51_out, not_52_out, not_53_out, not_54_out;

  not not_1 (not_1_out, Op5);
  not not_2 (not_2_out, Op4);
  not not_3 (not_3_out, Op3);
  not not_4 (not_4_out, Op1);
  not not_5 (not_5_out, Op5);
  not not_6 (not_6_out, Op4);
  not not_7 (not_7_out, Op3);
  not not_8 (not_8_out, Op5);
  not not_9 (not_9_out, Op4);
  not not_10 (not_10_out, Op1);
  not not_11 (not_11_out, Op5);
  not not_12 (not_12_out, Op4);
  not not_13 (not_13_out, Op0);
  not not_14 (not_14_out, Op5);
  not not_15 (not_15_out, Op4);
  not not_16 (not_16_out, Op2);
  not not_17 (not_17_out, Op5);
  not not_18 (not_18_out, Op4);
  not not_19 (not_19_out, Op3);
  not not_20 (not_20_out, Op5);
  not not_21 (not_21_out, Op4);
  not not_22 (not_22_out, Op2);
  not not_23 (not_23_out, Op5);
  not not_24 (not_24_out, Op4);
  not not_25 (not_25_out, Op0);
  not not_26 (not_26_out, Op5);
  not not_27 (not_27_out, Op4);
  not not_28 (not_28_out, Op1);
  not not_29 (not_29_out, Op5);
  not not_30 (not_30_out, Op4);
  not not_31 (not_31_out, Op3);
  not not_32 (not_32_out, Op0);
  not not_33 (not_33_out, Op5);
  not not_34 (not_34_out, Op4);
  not not_35 (not_35_out, Op2);
  not not_36 (not_36_out, Op5);
  not not_37 (not_37_out, Op4);
  not not_38 (not_38_out, Op2);
  not not_39 (not_39_out, Op4);
  not not_40 (not_40_out, Op3);
  not not_41 (not_41_out, Op1);
  not not_42 (not_42_out, Op0);
  not not_43 (not_43_out, Op4);
  not not_44 (not_44_out, Op2);
  not not_45 (not_45_out, Op1);
  not not_46 (not_46_out, Op0);
  not not_47 (not_47_out, Op4);
  not not_48 (not_48_out, Op2);
  not not_49 (not_49_out, Op5);
  not not_50 (not_50_out, Op4);
  not not_51 (not_51_out, Op3);
  not not_52 (not_52_out, Op5);
  not not_53 (not_53_out, Op4);
  not not_54 (not_54_out, Op2);
  and and_1 (and_1_out, not_1_out, not_2_out, not_3_out, not_4_out);
  and and_2 (and_2_out, not_5_out, not_6_out, not_7_out, Op2);
  and and_3 (and_3_out, not_8_out, not_9_out, Op2, not_10_out);
  and and_4 (and_4_out, not_11_out, not_12_out, Op2, not_13_out);
  and and_5 (and_5_out, not_14_out, not_15_out, Op3, not_16_out, Op1);
  and and_6 (and_6_out, not_17_out, not_18_out, not_19_out, Op2, Op1);
  and and_7 (and_7_out, not_20_out, not_21_out, Op3, not_22_out, Op1);
  and and_8 (and_8_out, not_23_out, not_24_out, Op3, Op1, not_25_out);
  and and_9 (and_9_out, not_26_out, not_27_out, Op2, not_28_out, Op0);
  and and_10 (and_10_out, not_29_out, not_30_out, not_31_out, Op2, Op1, not_32_out);
  and and_11 (and_11_out, not_33_out, not_34_out, Op3, not_35_out, Op0);
  and and_12 (and_12_out, not_36_out, not_37_out, Op3, not_38_out, Op1);
  and and_13 (and_13_out, Op5, not_39_out, not_40_out, not_41_out, not_42_out);
  and and_14 (and_14_out, Op5, not_43_out, not_44_out, not_45_out, not_46_out);
  and and_15 (and_15_out, Op5, not_47_out, not_48_out, Op1, Op0);
  and and_16 (and_16_out, not_49_out, not_50_out, not_51_out, Op2);
  and and_17 (and_17_out, not_52_out, not_53_out, Op3, not_54_out, Op1);
  or or_1 (ALU3, and_1_out, and_2_out, and_3_out, and_4_out, and_5_out);
  or or_2 (ALU2, and_6_out, and_7_out, and_8_out);
  or or_3 (ALU1, and_9_out, and_10_out, and_11_out, and_12_out, and_13_out, and_14_out, and_15_out);
  or or_4 (ALU0, and_16_out, and_17_out);
endmodule

// ALU special Ctrl
module ALU_special_ctrl (
  input  func5,
  input  func4,
  input  func3,
  input  func2,
  input  func1,
  input  func0,
  output ALU3,
  output ALU2,
  output ALU1,
  output ALU0
);

  wire and_1_out, and_2_out, and_3_out, and_5_out, not_1_out, not_2_out;

  and and_1 (and_1_out, func5, func2);
  not not_1 (not_1_out, func3);
  and and_2 (and_2_out, func3, func0);
  and and_3 (and_3_out, func5, func0);
  not not_2 (not_2_out, func5);
  or or_1 (ALU3, func3, and_1_out);
  and and_4 (ALU2, not_1_out, func1);
  or or_2 (ALU1, and_2_out, and_3_out);
  and and_5 (and_5_out, not_2_out, func1, func0);
  or or_3 (ALU0, and_5_out, func3);
endmodule

// ID/EX
module ID_EX_Pipeline_Register (
  input  [3:0] ALUOp,
  input  Branch,
  input  RegWrite,
  input  [4:0] WriteRegAddress,
  input  Comp,
  input  MemRead,
  input  MemtoReg,
  input  MemWrite,
  input  ALUSrc,
  input  Clock,
  input  [31:0] ReadData1,
  input  [31:0] ReadData2,
  input  [31:0] Imm,
  input  [4:0] Shamt,
  input  CompSelect,
  input  Mov,
  input  [4:0] Rs,
  input  [4:0] Rt,
  output [3:0] ALUOp_2,
  output Branch_2,
  output RegWrite_2,
  output [4:0] WriteRegAddress_2,
  output Comp_2,
  output MemRead_2,
  output MemtoReg_2,
  output MemWrite_2,
  output ALUSrc_2,
  output [31:0] ReadData1_2,
  output [31:0] ReadData2_2,
  output [31:0] Imm_2,
  output [4:0] Shamt_2,
  output CompSelect_2,
  output Mov_2,
  output [4:0] Rs_2,
  output [4:0] Rt_2
);

  Register #(.width(4)) u_ALUOp (.D(ALUOp), .Q(ALUOp_2), .clk(Clock));  // open: en, clr
  Register #(.width(1)) u_Branch (.D(Branch), .Q(Branch_2), .clk(Clock));  // open: en, clr
  Register #(.width(1)) u_RegWrite (.D(RegWrite), .Q(RegWrite_2), .clk(Clock));  // open: en, clr
  Register #(.width(5)) RegDst1 (.D(WriteRegAddress), .Q(WriteRegAddress_2), .clk(Clock));  // open: en, clr
  Register #(.width(1)) u_Comp (.D(Comp), .Q(Comp_2), .clk(Clock));  // open: en, clr
  Register #(.width(1)) u_MemRead (.D(MemRead), .Q(MemRead_2), .clk(Clock));  // open: en, clr
  Register #(.width(1)) u_MemtoReg (.D(MemtoReg), .Q(MemtoReg_2), .clk(Clock));  // open: en, clr
  Register #(.width(1)) u_MemWrite (.D(MemWrite), .Q(MemWrite_2), .clk(Clock));  // open: en, clr
  Register #(.width(1)) u_ALUSrc (.D(ALUSrc), .Q(ALUSrc_2), .clk(Clock));  // open: en, clr
  Register #(.width(32)) Read_Data_1 (.D(ReadData1), .Q(ReadData1_2), .clk(Clock));  // open: en, clr
  Register #(.width(32)) Read_Data_2 (.D(ReadData2), .Q(ReadData2_2), .clk(Clock));  // open: en, clr
  Register #(.width(32)) u_Imm (.D(Imm), .Q(Imm_2), .clk(Clock));  // open: en, clr
  Register #(.width(5)) u_Shamt (.D(Shamt), .Q(Shamt_2), .clk(Clock));  // open: en, clr
  Register #(.width(1)) register_1 (.D(CompSelect), .Q(CompSelect_2), .clk(Clock));  // open: en, clr
  Register #(.width(1)) register_2 (.D(Mov), .Q(Mov_2), .clk(Clock));  // open: en, clr
  Register #(.width(5)) u_Rs (.D(Rs), .Q(Rs_2), .clk(Clock));  // open: en, clr
  Register #(.width(5)) u_Rt (.D(Rt), .Q(Rt_2), .clk(Clock));  // open: en, clr
endmodule

// ALU Regimm Op
module ALU_Regimm_Ctrl (
  input  Bit_16,
  output [3:0] ALU_Op
);

  Multiplexer #(.width(4)) multiplexer_1 (.in0(4'b1101), .in1(4'b1111), .out(ALU_Op), .sel(Bit_16));  // open: en
endmodule

// MEM/WB
module EX_WB_Pipeline_Register (
  input  RegWrite,
  input  [4:0] RegWriteAddress,
  input  [31:0] Result,
  input  Clock,
  output RegWrite_2,
  output [4:0] RegWriteAddress_2,
  output [31:0] Result_2
);

  Register #(.width(1)) u_RegWrite (.D(RegWrite), .Q(RegWrite_2), .clk(Clock));  // open: en, clr
  Register #(.width(5)) u_RegWriteAddress (.D(RegWriteAddress), .Q(RegWriteAddress_2), .clk(Clock));  // open: en, clr
  Register #(.width(32)) u_Result (.D(Result), .Q(Result_2), .clk(Clock));  // open: en, clr
endmodule

module Forwarding (
  input  EX_Mem_RegWrite,
  input  [4:0] Ex_Mem_Rd,
  input  [4:0] ID_EX_Rs,
  input  [4:0] ID_EX_Rt,
  input  MEM_WB_RegWrite,
  input  [4:0] MEM_WB_Rd
);

  wire and_1_out, and_2_out, and_3_out, n5biteq_1_out, n5biteq_2_out, n5biteq_3_out, n5biteq_4_out,
       n5biteq_5_out, nand_1_out, not_1_out, not_2_out, not_3_out;

  _5bitEq u_5biteq_1 (.A(Ex_Mem_Rd), .B({5{1'b0}}), .Out(n5biteq_1_out));
  _5bitEq u_5biteq_2 (.A(ID_EX_Rt), .B(MEM_WB_Rd), .Out(n5biteq_2_out));
  _5bitEq u_5biteq_3 (.A(MEM_WB_Rd), .B({5{1'b0}}), .Out(n5biteq_3_out));
  not not_1 (not_1_out, n5biteq_4_out);
  not not_2 (not_2_out, n5biteq_1_out);
  not not_3 (not_3_out, n5biteq_3_out);
  nand nand_1 (nand_1_out, EX_Mem_RegWrite, not_2_out, not_1_out);
  _5bitEq u_5biteq_4 (.A(Ex_Mem_Rd), .B(ID_EX_Rs), .Out(n5biteq_4_out));
  _5bitEq u_5biteq_5 (.A(Ex_Mem_Rd), .B(ID_EX_Rt), .Out(n5biteq_5_out));
  and and_1 (and_1_out, EX_Mem_RegWrite, not_2_out, n5biteq_4_out);
  and and_2 (and_2_out, EX_Mem_RegWrite, not_2_out, n5biteq_5_out);
  and and_3 (and_3_out, MEM_WB_RegWrite, not_3_out, nand_1_out, n5biteq_2_out);
endmodule

module _5bitEq (
  input  [4:0] A,
  input  [4:0] B,
  output Out
);

  wire [4:0] xnor_1_out;

  assign xnor_1_out = ~(A ^ B);  // XNOR_Gate xnor_1, 5 bits wide
  and and_1 (Out, xnor_1_out[0], xnor_1_out[1], xnor_1_out[2], xnor_1_out[3], xnor_1_out[4]);
endmodule

// Forward
module ForwardCtrl (
  input  XMRegWrite,
  input  MWRegWrite,
  input  [4:0] XMRd,
  input  [4:0] DXRs,
  input  [4:0] DXRt,
  input  [4:0] MWRd,
  output [1:0] FA,
  output [1:0] FB
);

  wire exhazard_1_exforwarda, exhazard_1_exforwardb, n5biteq_1_out, n5biteq_2_out, n5biteq_3_out,
       n5biteq_4_out, n5biteq_5_out, n5biteq_6_out, not_1_out, not_2_out;

  _5bitEq u_5biteq_1 (.A(XMRd), .B(DXRs), .Out(n5biteq_1_out));
  _5bitEq u_5biteq_2 (.A(XMRd), .B(DXRt), .Out(n5biteq_2_out));
  not not_1 (not_1_out, n5biteq_3_out);
  _5bitEq u_5biteq_3 (.A(MWRd), .B({5{1'b0}}), .Out(n5biteq_3_out));
  _5bitEq u_5biteq_4 (.A(XMRd), .B({5{1'b0}}), .Out(n5biteq_4_out));
  not not_2 (not_2_out, n5biteq_4_out);
  _5bitEq u_5biteq_5 (.A(DXRt), .B(MWRd), .Out(n5biteq_5_out));
  _5bitEq u_5biteq_6 (.A(DXRs), .B(MWRd), .Out(n5biteq_6_out));
  EXHazard exhazard_1 (
    .XMRegWrite(XMRegWrite), .XMRdneq0(not_2_out), .XMRdeqDXRs(n5biteq_1_out), .XMRdeqDXRt(n5biteq_2_out),
    .ExForwardA(exhazard_1_exforwarda), .ExForwardB(exhazard_1_exforwardb));
  MemHazard memhazard_1 (
    .MWRegWrite(MWRegWrite), .MWRdneq0(not_1_out), .ExHazardA(exhazard_1_exforwarda),
    .ExHazardB(exhazard_1_exforwardb), .MWRdeqDXRs(n5biteq_6_out), .MWRdeqDXRt(n5biteq_5_out), .FA1(FA[1]),
    .FA2(FA[0]), .FB1(FB[1]), .FB2(FB[0]));
endmodule

module EXHazard (
  input  XMRegWrite,
  input  XMRdneq0,
  input  XMRdeqDXRs,
  input  XMRdeqDXRt,
  output ExForwardA,
  output ExForwardB
);

  and and_1 (ExForwardA, XMRegWrite, XMRdneq0, XMRdeqDXRs);
  and and_2 (ExForwardB, XMRegWrite, XMRdneq0, XMRdeqDXRt);
endmodule

module MemHazard (
  input  MWRegWrite,
  input  MWRdneq0,
  input  ExHazardA,
  input  ExHazardB,
  input  MWRdeqDXRs,
  input  MWRdeqDXRt,
  output FA1,
  output FA2,
  output FB1,
  output FB2
);

  wire not_1_out, not_2_out;

  not not_1 (not_1_out, ExHazardA);
  not not_2 (not_2_out, ExHazardB);
  and and_1 (FA2, MWRegWrite, MWRdneq0, not_1_out, MWRdeqDXRs);
  and and_2 (FB2, MWRegWrite, MWRdneq0, not_2_out, MWRdeqDXRt);

  assign FA1 = ExHazardA;
  assign FB1 = ExHazardB;
endmodule

// EX/MEM
module EX_MEM_Pipeline_Register (
  input  RegWrite,
  input  [4:0] RegWriteAddress,
  input  [31:0] Result,
  input  Clock,
  output RegWrite_2,
  output [4:0] RegWriteAddress_2,
  output [31:0] Result_2
);

  Register #(.width(1)) u_RegWrite (.D(RegWrite), .Q(RegWrite_2), .clk(Clock));  // open: en, clr
  Register #(.width(5)) u_RegWriteAddress (.D(RegWriteAddress), .Q(RegWriteAddress_2), .clk(Clock));  // open: en, clr
  Register #(.width(32)) u_Result (.D(Result), .Q(Result_2), .clk(Clock));  // open: en, clr
endmodule

// Shamt Ctrl
module Shamt (
  input  LUI,
  input  Shamtchoose,
  input  [4:0] A,
  input  [4:0] _6_10,
  output [4:0] Shamt
);

  wire [4:0] multiplexer_1_out;

  Multiplexer #(.width(5)) multiplexer_1 (
    .in0(A), .in1(_6_10), .out(multiplexer_1_out), .sel(Shamtchoose));  // open: en
  Multiplexer #(.width(5)) multiplexer_2 (.in0(multiplexer_1_out), .in1(5'b10000), .out(Shamt), .sel(LUI));  // open: en
endmodule
